// Logisim project ALU32Nhan.circ as structural Verilog
module ALU32 (
  input  [31:0] A,
  input  [31:0] B,
  input  [3:0] Op,
  input  [4:0] Sa,
  output [31:0] C,
  output V
);

  wire [31:0] addsubtractcirc_1_c, comparecirc_1_c, gatecirc_1_c, shiftcirc_1_c;

  GateCirc gatecirc_1 (.A(A), .B(B), .Op(Op), .C(gatecirc_1_c));
  CompareCirc comparecirc_1 (.B(B), .A(A), .Op(Op), .C(comparecirc_1_c));
  ShiftCirc shiftcirc_1 (.B(B), .Op(Op), .Sa(Sa), .C(shiftcirc_1_c));
  AddSubtractCirc addsubtractcirc_1 (.A(A), .Op(Op), .B(B), .V(V), .C(addsubtractcirc_1_c));
  assign C = gatecirc_1_c | comparecirc_1_c | addsubtractcirc_1_c | shiftcirc_1_c;  // OR_Gate or_1, 32 bits wide
endmodule

module LeftShift32 (
  input  [31:0] B,
  input  Cin,
  input  [4:0] Sa,
  output [31:0] C
);

  wire [31:0] multiplexer_1_out, multiplexer_2_out, multiplexer_3_out, multiplexer_4_out, shift1bit_1_c,
       shift2bit_1_c, shift4bit_1_c, shift8bit_1_c, shift16bit_1_c;

  Shift1bit shift1bit_1 (.Cin(Cin), .B(B), .C(shift1bit_1_c));
  Multiplexer #(.width(32), .enable("false")) multiplexer_1 (
    .in0(B), .in1(shift1bit_1_c), .out(multiplexer_1_out), .sel(Sa[0]));
  Shift2bit shift2bit_1 (.C(shift2bit_1_c), .Cin(Cin), .B(multiplexer_1_out));
  Multiplexer #(.width(32), .enable("false")) multiplexer_2 (
    .in0(multiplexer_1_out), .in1(shift2bit_1_c), .out(multiplexer_2_out), .sel(Sa[1]));
  Shift4bit shift4bit_1 (.C(shift4bit_1_c), .Cin(Cin), .B(multiplexer_2_out));
  Multiplexer #(.width(32), .enable("false")) multiplexer_3 (
    .in0(multiplexer_2_out), .in1(shift4bit_1_c), .out(multiplexer_3_out), .sel(Sa[2]));
  Shift8bit shift8bit_1 (.C(shift8bit_1_c), .Cin(Cin), .B(multiplexer_3_out));
  Multiplexer #(.width(32), .enable("false")) multiplexer_4 (
    .in0(multiplexer_3_out), .in1(shift8bit_1_c), .out(multiplexer_4_out), .sel(Sa[3]));
  Shift16bit shift16bit_1 (.C(shift16bit_1_c), .in_1(Cin), .B(multiplexer_4_out));
  Multiplexer #(.width(32), .enable("false")) multiplexer_5 (
    .in0(multiplexer_4_out), .in1(shift16bit_1_c), .out(C), .sel(Sa[4]));
endmodule

module Add32 (
  input  [31:0] A,
  input  [31:0] B,
  input  Cin,
  output V,
  output [31:0] C
);

  wire add16bit_1_cout, add16bit_2_cout, add16bit_2_overflow;

  Add16bit add16bit_1 (.A(A[15:0]), .B(B[15:0]), .Cin(Cin), .Cout(add16bit_1_cout), .S(C[15:0]));  // open: overflow
  Add16bit add16bit_2 (
    .A(A[31:16]), .B(B[31:16]), .Cin(add16bit_1_cout), .Cout(add16bit_2_cout),
    .overflow(add16bit_2_overflow), .S(C[31:16]));
  xor xor_1 (V, add16bit_2_cout, add16bit_2_overflow);
endmodule

module Mirror (
  input  [31:0] B,
  output [31:0] Mirror_B,
  output SignBit
);


  assign Mirror_B = {B[0], B[1], B[2], B[3], B[4], B[5], B[6], B[7], B[8], B[9], B[10], B[11], B[12], B[13], B[14], B[15], B[16], B[17], B[18], B[19], B[20], B[21], B[22], B[23], B[24], B[25], B[26], B[27], B[28], B[29], B[30], B[31]};
  assign SignBit = B[31];

  // Notes on the sheet:
  //   I use a sub circuit since it is very large.
endmodule

module AddSubtractCirc (
  input  [31:0] A,
  input  [3:0] Op,
  input  [31:0] B,
  output V,
  output [31:0] C
);

  wire and_1_out, and_2_out;
  wire [31:0] and_3_out, and_4_out, bit_extender_1_out, bit_extender_2_out, xor_1_out;

  and and_1 (and_1_out, Op[1], ~Op[3]);  // AND_Gate
  assign bit_extender_1_out = {{31{Op[2]}}, Op[2]};  // Bit_Extender bit_extender_1
  assign bit_extender_2_out = {{31{and_1_out}}, and_1_out};  // Bit_Extender bit_extender_2
  assign xor_1_out = bit_extender_1_out ^ B;  // XOR_Gate xor_1, 32 bits wide
  and and_2 (and_2_out, and_1_out, Op[2]);
  assign and_3_out = A & bit_extender_2_out;  // AND_Gate and_3, 32 bits wide
  assign and_4_out = bit_extender_2_out & xor_1_out;  // AND_Gate and_4, 32 bits wide
  Add32 add32_1 (.A(and_3_out), .B(and_4_out), .Cin(and_2_out), .V(V), .C(C));
endmodule

module CompareCirc (
  input  [31:0] B,
  input  [31:0] A,
  input  [3:0] Op,
  output [31:0] C
);

  wire and_1_out, and_4_out, and_7_out, and_8_out, and_9_out, not_2_out, not_3_out, or_1_out;
  wire [1:0] and_5_out, and_6_out;
  wire [7:0] and_2_out, and_3_out;
  wire [31:0] bit_extender_1_out, bit_extender_2_out, bit_extender_3_out, bit_extender_4_out, not_1_out,
       xnor_1_out;

  assign not_1_out = ~A;  // NOT_Gate not_1, 32 bits wide
  assign xnor_1_out = ~(B ^ A);  // XNOR_Gate xnor_1, 32 bits wide
  and and_1 (and_1_out, Op[3], Op[2], Op[1]);
  assign and_2_out = xnor_1_out[7:0] & xnor_1_out[15:8] & xnor_1_out[23:16] & xnor_1_out[31:24];  // AND_Gate and_2, 8 bits wide
  assign and_3_out = not_1_out[7:0] & not_1_out[15:8] & not_1_out[23:16] & not_1_out[31:24];  // AND_Gate and_3, 8 bits wide
  and and_4 (and_4_out, ~Op[1], ~Op[2], Op[3]);  // AND_Gate
  assign and_5_out = and_3_out[1:0] & and_3_out[3:2] & and_3_out[5:4] & and_3_out[7:6];  // AND_Gate and_5, 2 bits wide
  assign and_6_out = and_2_out[1:0] & and_2_out[3:2] & and_2_out[5:4] & and_2_out[7:6];  // AND_Gate and_6, 2 bits wide
  and and_7 (and_7_out, and_5_out[0], and_5_out[1]);
  or or_1 (or_1_out, and_4_out, and_1_out);
  and and_8 (and_8_out, and_6_out[0], and_6_out[1]);
  and and_9 (and_9_out, ~A[31], ~and_7_out);  // AND_Gate
  assign bit_extender_1_out = {{31{1'b0}}, and_9_out};  // Bit_Extender bit_extender_1
  not not_2 (not_2_out, and_9_out);
  assign bit_extender_2_out = {{31{1'b0}}, not_2_out};  // Bit_Extender bit_extender_2
  assign bit_extender_3_out = {{31{1'b0}}, and_8_out};  // Bit_Extender bit_extender_3
  assign bit_extender_4_out = {{31{1'b0}}, not_3_out};  // Bit_Extender bit_extender_4
  not not_3 (not_3_out, and_8_out);
  Multiplexer #(.select(2), .width(32)) multiplexer_1 (
    .in0(bit_extender_4_out), .in1(bit_extender_3_out), .in2(bit_extender_2_out), .in3(bit_extender_1_out),
    .out(C), .sel(Op[1:0]), .en(or_1_out));

  // Notes on the sheet:
  //   If A==B, then A XNOR B is 1
  //   If A>0, then A's 31th bit is 0
  //   If A>0, then there exists 1 bit from 0 to 30th that is equal to 1
  //   If the OpCode is not CompareCirc, then C is 0
endmodule

module ShiftCirc (
  input  [31:0] B,
  input  [3:0] Op,
  input  [4:0] Sa,
  output [31:0] C
);

  wire and_1_out, and_2_out, and_3_out, and_4_out, mirror_1_signbit, or_1_out;
  wire [4:0] and_5_out, bit_extender_1_out;
  wire [31:0] leftshift32_1_c, mirror_1_mirror_b, mirror_2_mirror_b, multiplexer_1_out;

  and and_1 (and_1_out, ~Op[1], Op[2], Op[3]);  // AND_Gate
  and and_2 (and_2_out, ~Op[3], ~Op[2], ~Op[1]);  // AND_Gate
  Mirror mirror_1 (.B(B), .Mirror_B(mirror_1_mirror_b), .SignBit(mirror_1_signbit));
  and and_3 (and_3_out, mirror_1_signbit, Op[0]);
  Multiplexer #(.width(32)) multiplexer_1 (
    .in0(B), .in1(mirror_1_mirror_b), .out(multiplexer_1_out), .sel(Op[2]), .en(or_1_out));
  or or_1 (or_1_out, and_2_out, and_1_out);
  assign bit_extender_1_out = {{4{or_1_out}}, or_1_out};  // Bit_Extender bit_extender_1
  and and_4 (and_4_out, and_3_out, Op[2]);
  assign and_5_out = bit_extender_1_out & Sa;  // AND_Gate and_5, 5 bits wide
  LeftShift32 leftshift32_1 (.B(multiplexer_1_out), .Cin(and_4_out), .Sa(and_5_out), .C(leftshift32_1_c));
  Mirror mirror_2 (.B(leftshift32_1_c), .Mirror_B(mirror_2_mirror_b));  // open: SignBit
  Multiplexer #(.width(32), .enable("false")) multiplexer_2 (
    .in0(leftshift32_1_c), .in1(mirror_2_mirror_b), .out(C), .sel(Op[2]));
endmodule

module Shift1bit (
  input  Cin,
  input  [31:0] B,
  output [31:0] C
);


  assign C = {B[30:0], Cin};
endmodule

module Shift2bit (
  input  Cin,
  input  [31:0] B,
  output [31:0] C
);

  wire [31:0] shift1bit_1_c;

  Shift1bit shift1bit_1 (.Cin(Cin), .B(B), .C(shift1bit_1_c));
  Shift1bit shift1bit_2 (.Cin(Cin), .B(shift1bit_1_c), .C(C));
endmodule

module Shift4bit (
  input  Cin,
  input  [31:0] B,
  output [31:0] C
);

  wire [31:0] shift2bit_1_c;

  Shift2bit shift2bit_1 (.C(shift2bit_1_c), .Cin(Cin), .B(B));
  Shift2bit shift2bit_2 (.C(C), .Cin(Cin), .B(shift2bit_1_c));
endmodule

module Shift8bit (
  input  Cin,
  input  [31:0] B,
  output [31:0] C
);

  wire [31:0] shift4bit_1_c;

  Shift4bit shift4bit_1 (.C(shift4bit_1_c), .Cin(Cin), .B(B));
  Shift4bit shift4bit_2 (.C(C), .Cin(Cin), .B(shift4bit_1_c));
endmodule

module Shift16bit (
  input  in_1,
  input  [31:0] B,
  output [31:0] C
);

  wire [31:0] shift8bit_1_c;

  Shift8bit shift8bit_1 (.C(shift8bit_1_c), .Cin(in_1), .B(B));
  Shift8bit shift8bit_2 (.C(C), .Cin(in_1), .B(shift8bit_1_c));
endmodule

module Add1bit (
  input  A,
  input  B,
  input  Cin,
  output S,
  output Cout
);

  wire and_1_out, and_2_out, xor_1_out;

  xor xor_1 (xor_1_out, A, B);
  and and_1 (and_1_out, A, B);
  and and_2 (and_2_out, xor_1_out, Cin);
  xor xor_2 (S, xor_1_out, Cin);
  or or_1 (Cout, and_2_out, and_1_out);
endmodule

module Add4bit (
  input  [3:0] A,
  input  [3:0] B,
  input  Cin,
  output Cout,
  output overflow,
  output [3:0] S
);

  wire add1bit_1_cout, add1bit_2_cout;

  Add1bit add1bit_1 (.A(A[0]), .B(B[0]), .Cin(Cin), .S(S[0]), .Cout(add1bit_1_cout));
  Add1bit add1bit_2 (.A(A[1]), .B(B[1]), .Cin(add1bit_1_cout), .S(S[1]), .Cout(add1bit_2_cout));
  Add1bit add1bit_3 (.A(A[2]), .B(B[2]), .Cin(add1bit_2_cout), .S(S[2]), .Cout(overflow));
  Add1bit add1bit_4 (.A(A[3]), .B(B[3]), .Cin(overflow), .S(S[3]), .Cout(Cout));
endmodule

module Add16bit (
  input  [15:0] A,
  input  [15:0] B,
  input  Cin,
  output Cout,
  output overflow,
  output [15:0] S
);

  wire add4bit_1_cout, add4bit_2_cout, add4bit_3_cout;

  Add4bit add4bit_1 (.A(A[3:0]), .B(B[3:0]), .Cin(Cin), .Cout(add4bit_1_cout), .S(S[3:0]));  // open: overflow
  Add4bit add4bit_2 (
    .A(A[7:4]), .B(B[7:4]), .Cin(add4bit_1_cout), .Cout(add4bit_2_cout), .S(S[7:4]));  // open: overflow
  Add4bit add4bit_3 (
    .A(A[11:8]), .B(B[11:8]), .Cin(add4bit_2_cout), .Cout(add4bit_3_cout), .S(S[11:8]));  // open: overflow
  Add4bit add4bit_4 (.A(A[15:12]), .B(B[15:12]), .Cin(add4bit_3_cout), .Cout(Cout), .overflow(overflow), .S(S[15:12]));
endmodule

module GateCirc (
  input  [31:0] A,
  input  [31:0] B,
  input  [3:0] Op,
  output [31:0] C
);

  wire and_1_out, and_2_out, or_2_out;
  wire [31:0] and_3_out, not_1_out, or_1_out, xor_1_out;

  and and_1 (and_1_out, Op[3], ~Op[2], Op[1]);  // AND_Gate
  and and_2 (and_2_out, ~Op[3], Op[2], ~Op[1]);  // AND_Gate
  assign and_3_out = A & B;  // AND_Gate and_3, 32 bits wide
  assign or_1_out = A | B;  // OR_Gate or_1, 32 bits wide
  assign xor_1_out = A ^ B;  // XOR_Gate xor_1, 32 bits wide
  assign not_1_out = ~or_1_out;  // NOT_Gate not_1, 32 bits wide
  or or_2 (or_2_out, and_1_out, and_2_out);
  Multiplexer #(.select(2), .width(32)) multiplexer_1 (
    .in0(and_3_out), .in1(or_1_out), .in2(xor_1_out), .in3(not_1_out), .out(C), .sel(Op[1:0]), .en(or_2_out));
endmodule
